# Fritzing sketch air-quality-clock (saved by Fritzing 0.9.5d)

parts:
  Компонент1 = Arduino Nano (Rev3.0)
  R1 = Resistor [tolerance=±5% resistance=1k package=THT]
  R3 = Resistor [tolerance=±5% resistance=1k package=THT]
  R4 = Resistor [tolerance=±5% resistance=1k package=THT]
  R5 = Resistor [tolerance=±5% resistance=1k package=THT]
  R2 = Resistor [tolerance=±5% resistance=1k package=THT]
  R6 = Photocell (LDR) [package=THT]
  R7 = Trimmer Potentiometer [maximum_resistance=500Ω package=THT]
  U1 = Keystudio SEN-CCS811
  R8 = Resistor [tolerance=±5% resistance=10k package=THT]
  J1 = Piezo Speaker
  R9 = Resistor [tolerance=±5% resistance=10k package=THT]
  R10 = Resistor [tolerance=±5% resistance=10k package=THT]
  R11 = Resistor [tolerance=±5% resistance=10k package=THT]
  R12 = Resistor [tolerance=±5% resistance=10k package=THT]
  C2 = Tantalum Capacitor [capacitance=1μF package="100 mil [THT, tantalum]"]
  C3 = Tantalum Capacitor [capacitance=1μF package="100 mil [THT, tantalum]"]
  C4 = Tantalum Capacitor [capacitance=1μF package="100 mil [THT, tantalum]"]
  LED1 = RGB LED (com. cathode, rgb) [package="5 mm [THT]"]
  R13 = Resistor [tolerance=±5% resistance=680 package=THT]
  R14 = Resistor [tolerance=±5% resistance=680 package=THT]
  R15 = Resistor [tolerance=±5% resistance=680 package=THT]
  R16 = Resistor [tolerance=±5% resistance=10k package=THT]
  R17 = Resistor [tolerance=±5% resistance=3.6k package=THT]
  U3 = SWITCH_SPDT [package=kps-1290]
  Компонент2 = BME280 Breakout
  ZS-042_RTC1 = ZS-042 RTC Module
  Компонент3 = Max Power IR LED Kit
  LCD1 = LCD TFT 1.8" 128x160 (ST7735S)
  TD-er1 = MH-Z19 CO2 sensor [part_number=MH-Z19]
  U4 = MP503 (ZP07)
  U5 = Navigation Switch [package=nav_switch]
  Компонент4 = JeePlug experimenter's board
  Компонент5 = Lithium Ion Cylindrical Battery 3.7v 2200mAh [part_number=1781]
  AMS1 = AMS1777 5V regulator module
  AMS2 = AMS1777 5V regulator module
  U6 = SWITCH_SPDT [package=kps-1290]
  U7 = SWITCH_SPDT [package=kps-1290]

nets:
  N1: Компонент1.RESET, R5.Pin_0, U1.connector4
  GND: Компонент1.GND, LCD1.GND, Компонент4.B1, Компонент5.negative, AMS1.GND-_(output), AMS2.GND-_(output)
  N2: Компонент1.D2, R12.Pin_1, C2.+, U5.1
  N3: Компонент1.D3, TD-er1.TX
  N4: Компонент1.D4, TD-er1.Vout, TD-er1.RX
  N5: Компонент1.D5, R13.Pin_0
  N6: Компонент1.D6, R11.Pin_1, C3.+, U5.2
  N7: Компонент1.D7, U4.connector0
  N8: Компонент1.D8, U4.connector1
  N9: Компонент1.D9, R14.Pin_0
  N10: Компонент1.D10, R15.Pin_0
  N11: Компонент1.D11/MOSI, R2.Pin_0
  N12: Компонент1.D12/MISO, R10.Pin_1, C4.+, U5.C
  N13: Компонент1.VIN, U3.P, AMS1.VIN+
  N14: Компонент1.5V, U6.O, U7.O
  N15: Компонент1.A7, R16.Pin_1, R17.Pin_0
  N16: Компонент1.A5, U1.connector3, Компонент2.SCK/SCL, ZS-042_RTC1.SCL
  N17: Компонент1.A4, U1.connector2, Компонент2.SDI/SDA, ZS-042_RTC1.SDA
  N18: Компонент1.A3, Компонент3.CONTROL
  N19: Компонент1.A2, R3.Pin_0
  N20: Компонент1.A1, R4.Pin_0
  N21: Компонент1.A0, Компонент1.AREF, R9.Pin_0
  N22: Компонент1.3V3, U1.connector5
  N23: Компонент1.D13/SCK, R1.Pin_0
  N24: R1.Pin_1, LCD1.CLK/SCK/SCL
  N25: R3.Pin_1, LCD1.CS
  N26: R4.Pin_1, LCD1.RS/DC
  N27: R5.Pin_1, LCD1.RST
  N28: R2.Pin_1, LCD1.SDA/MOSI
  N29: R6.pin_0, R7.leg1, LCD1.BLK
  N30: R6.pin_1, LCD1.VCC, Компонент4.N$24, U7.P
  N31: R7.wiper, LED1.red_anode, R16.Pin_0, Компонент4.B2
  N32: U1.connector0, TD-er1.GND, Компонент4.B4
  N33: U1.connector1, R8.Pin_1, Компонент4.A3, AMS1.VOUT+
  N34: U1.connector6, R8.Pin_0
  N35: J1.pin1, Компонент3.GND, Компонент4.B3
  N36: J1.pin2, R9.Pin_1
  N37: R10.Pin_0, R11.Pin_0, R12.Pin_0, Компонент2.3.3V, Компонент4.A6
  N38: C2.-, ZS-042_RTC1.GND, Компонент4.B6
  N39: C3.-, C4.-, U5.T
  N40: LED1.common_cathode, R13.Pin_1
  N41: LED1.green_anode, R14.Pin_1
  N42: LED1.blue_anode, R15.Pin_1
  N43: R17.Pin_1, U3.S, Компонент5.positive, U6.S
  N44: Компонент2.GND, U4.connector3, Компонент4.B5
  N45: ZS-042_RTC1.VCC, Компонент4.A5, AMS2.VOUT+
  N46: Компонент3.VCC, Компонент4.A1
  N47: TD-er1.Vin, Компонент4.A2
  N48: U4.connector2, Компонент4.A4
  N49: AMS1.GND-_(input), AMS2.GND-_(input)
  N50: AMS2.VIN+, U6.P

notes:
  Выход контроллера заряда на 2 банки, 7.4 вольта
  3.3V
  5.0V
  7.2V
  2S Controller
  Battery
  USB

custom parts:
  Keystudio SEN-CCS811: Keystudio SEN-CCS811 Air quality sensor
  Lithium Ion Cylindrical Battery 3.7v 2200mAh: This lithium ion battery has a capacity of 2200mAh and a protection circuit that provides over-voltage, under-voltage and over-current protection. This cell can provide 2C of peak current (4400mA). Note that these batteries are not designed to sustain such high loads, we suggest keeping any constant current draw under about 0.5C (1 Amp).
  AMS1777 5V regulator module: AMS1777 5V regulator module source : https://github.com/ShenTengTu/fritzing_parts/tree/master/voltage%20regulator/AMS1117_5V_regulator_module
